# Fritzing sketch sesame (saved by Fritzing 0.9.3b)

parts:
  Arduino = Arduino Uno (Rev3) - ICSP
  MFRC522 = RFID-RC522-v3
  Relay = Keyes Relay [package=THT]
  LED1 = RGB LED (com. anode, rbg) [package="5 mm [THT]"]
  R1 = Resistor [tolerance=±5% resistance=100 package="0805 [SMD]"]

nets:
  N1: Arduino.ICSP_MISO, Arduino.D12/MISO, MFRC522.MISO, Relay.signal
  N2: Arduino.5V, Relay.power, R1.Pin_1
  N3: Arduino.ICSP_SCK, MFRC522.SCK
  N4: Arduino.ICSP_MOSI, Arduino.D11_PWM/MOSI, MFRC522.MOSI
  N5: Arduino.RESET, MFRC522.RST
  GND: Arduino.GND, MFRC522.GND, Relay.ground
  N6: Arduino.D10_PWM/SS, MFRC522.SDA
  N7: Arduino.D3_PWM, LED1.red_cathode
  N8: Arduino.D5_PWM, LED1.green_cathode
  N9: Arduino.D6_PWM, LED1.blue_cathode
  3V3: Arduino.3V3, MFRC522.3.3V
  N10: LED1.common_anode, R1.Pin_0

custom parts:
  RFID-RC522-v3: A simple China made RFID-RC522 Reader (6x4 cm); do check the pin labels, as this is a MFRC522 based clone.
  Keyes Relay: The Keyes 5V relay module is suitable for SCM development, home appliance control. It uses a 5V~12V TIL control signal which can control DC / AC signal.
